// Digital circuit computer_toy.dig as structural Verilog
module computer_toy (
  input  Reset,
  input  Set_D,
  input  Save_ACC,
  input  Load_ACC,
  input  Set_H,
  input  Load_H,
  input  In_0,
  input  In_1,
  input  In_2,
  input  In_3,
  input  In_4,
  input  In_5,
  input  In_6,
  input  In_7,
  input  Load_In,
  input  Load_M,
  input  Set_M,
  input  Set_L,
  input  Load_L,
  input  [7:0] Carry,
  input  Set_A,
  input  Set_T,
  input  Load_T,
  input  _0,
  input  _1,
  input  _1_2,
  input  X,
  input  Y,
  input  X_2,
  input  Y_2,
  input  X_plus_1,
  input  Y_plus_1,
  input  X_3,
  input  Y_3,
  input  X_1,
  input  Y_1,
  input  X_plus_Y,
  input  X_Y,
  input  Y_X,
  input  Y_X_2,
  input  Y_X_3,
  input  Set_PC_H,
  input  Set_PC_L,
  input  Set_PC,
  input  Clock,
  input  Load_ROM,
  output [7:0] ALU,
  output [7:0] D,
  output [7:0] ACC,
  output [7:0] H,
  output [7:0] In,
  output [7:0] Bus,
  output [7:0] M,
  output [7:0] L,
  output [15:0] A,
  output [7:0] T,
  output [15:0] PC,
  output [7:0] ROM
);

  wire nm_alu_hack8_1_c_out, nm_alu_hack8_1_ng, nm_alu_hack8_1_zr, nm_hack_opflag_decoder_1_f,
       nm_hack_opflag_decoder_1_no, nm_hack_opflag_decoder_1_nx, nm_hack_opflag_decoder_1_ny,
       nm_hack_opflag_decoder_1_zx, nm_hack_opflag_decoder_1_zy;
  wire [15:0] nm_byte_resetn_2_out;

  nm_byte_resetn nm_byte_resetn_1 (
    .D(Bus), .clk(Set_PC_H), .reset(Reset), .Out(nm_byte_resetn_2_out[15:8]));  // open: Out_2
  nm_byte_resetn nm_byte_resetn_2 (
    .D(Bus), .clk(Set_PC_L), .reset(Reset), .Out(nm_byte_resetn_2_out[7:0]));  // open: Out_2
  nm_counter16_resetn nm_counter16_resetn_1 (
    .D(nm_byte_resetn_2_out), .clk(Clock), .set(Set_PC), .reset(Reset), .Out(PC));  // open: ovf
  nm_enable8 nm_enable8_1 (.In({In_7, In_6, In_5, In_4, In_3, In_2, In_1, In_0}), .en(Load_In), .Out(Bus));
  ROM #(.AddrBits(16), .Bits(8)) rom_1 (.A(PC), .sel(1'b1), .D(ROM));
  nm_enable8 nm_enable8_2 (.In(ROM), .en(Load_ROM), .Out(Bus));
  nm_byte_resetn nm_byte_resetn_3 (.D(Bus), .clk(Set_D), .reset(Reset), .Out(D));  // open: Out_2
  nm_ALU_HACK8 nm_alu_hack8_1 (
    .X(D), .Y(Bus), .c_in(Carry), .Out(ALU), .zr(nm_alu_hack8_1_zr), .ng(nm_alu_hack8_1_ng),
    .c_out(nm_alu_hack8_1_c_out), .zx(nm_hack_opflag_decoder_1_zx), .nx(nm_hack_opflag_decoder_1_nx),
    .zy(nm_hack_opflag_decoder_1_zy), .ny(nm_hack_opflag_decoder_1_ny), .f(nm_hack_opflag_decoder_1_f),
    .no(nm_hack_opflag_decoder_1_no));
  nm_HACK_opflag_decoder nm_hack_opflag_decoder_1 (
    ._0(_0), ._1(_1), ._1_2(_1_2), .X(X), .Y(Y), .X_2(X_2), .Y_2(Y_2), .X_3(X_3), .Y_3(Y_3),
    .X_plus_1(X_plus_1), .Y_plus_1(Y_plus_1), .X_1(X_1), .Y_1(Y_1), .X_plus_Y(X_plus_Y), .X_Y(X_Y),
    .Y_X(Y_X), .Y_X_2(Y_X_2), .Y_X_3(Y_X_3), .zx(nm_hack_opflag_decoder_1_zx),
    .nx(nm_hack_opflag_decoder_1_nx), .zy(nm_hack_opflag_decoder_1_zy), .ny(nm_hack_opflag_decoder_1_ny),
    .f(nm_hack_opflag_decoder_1_f), .no(nm_hack_opflag_decoder_1_no));
  LED Zero (.in(nm_alu_hack8_1_zr));
  LED Negative (.in(nm_alu_hack8_1_ng));
  LED u_Carry (.in(nm_alu_hack8_1_c_out));
  nm_reg8_resetn nm_reg8_resetn_1 (.D(ALU), .clk(Save_ACC), .reset(Reset), .en(Load_ACC), .Out(Bus), .V(ACC));
  nm_reg8_resetn nm_reg8_resetn_2 (.D(Bus), .clk(Set_H), .reset(Reset), .en(Load_H), .Out(Bus), .V(H));
  nm_reg8_resetn nm_reg8_resetn_3 (.D(Bus), .clk(Set_L), .reset(Reset), .en(Load_L), .Out(Bus), .V(L));
  nm_reg8_resetn nm_reg8_resetn_4 (.D(Bus), .clk(Set_T), .reset(Reset), .en(Load_T), .Out(Bus), .V(T));
  nm_byte2_resetn nm_byte2_resetn_1 (.D({H, L}), .clk(Set_A), .reset(Reset), .Out(A));  // open: Out_2
  RAMAsync #(.AddrBits(16), .Bits(8)) ramasync_1 (.A(A), .D(Bus), .we(Set_M), .Q(M));
  nm_enable8 nm_enable8_3 (.In(M), .en(Load_M), .Out(Bus));
  // Pins of 1 and 8 bits meet at Carry

  assign In = {In_7, In_6, In_5, In_4, In_3, In_2, In_1, In_0};

  // Notes on the sheet:
  //   X_plus_Y: default 1
  //   contents of rom_1 (hex, n*v repeats v):
  //   de,ad,be,ef
endmodule
